// Logisim project datapath.circ as structural Verilog: 1 circuit, main circuit main
module main (
  input  [3:0] x0,
  input  [3:0] x1,
  input  [3:0] x2,
  input  [3:0] x3
);

  wire comparator_1_lt;
  wire [3:0] multiplexer_1_out, multiplexer_2_out, multiplexer_3_out, multiplexer_4_out, multiplexer_5_out,
       multiplexer_6_out, R0_q, R1_q, R2_q, R3_q;

  Multiplexer #(.width(4), .enable("false")) multiplexer_1 (
    .in0(x0), .in1(multiplexer_6_out), .out(multiplexer_1_out));  // open: sel
  Multiplexer #(.width(4), .enable("false")) multiplexer_2 (
    .in0(x1), .in1(multiplexer_5_out), .out(multiplexer_2_out));  // open: sel
  Multiplexer #(.width(4), .enable("false")) multiplexer_3 (
    .in0(x2), .in1(multiplexer_6_out), .out(multiplexer_3_out));  // open: sel
  Multiplexer #(.width(4), .enable("false")) multiplexer_4 (
    .in0(x3), .in1(multiplexer_5_out), .out(multiplexer_4_out));  // open: sel
  Register #(.width(4)) R0 (.D(multiplexer_1_out), .Q(R0_q));  // open: en, clk, clr
  Register #(.width(4)) R1 (.D(multiplexer_2_out), .Q(R1_q));  // open: en, clk, clr
  Register #(.width(4)) R2 (.D(multiplexer_3_out), .Q(R2_q));  // open: en, clk, clr
  Register #(.width(4)) R3 (.D(multiplexer_4_out), .Q(R3_q));  // open: en, clk, clr
  Multiplexer #(.width(4), .enable("false")) multiplexer_5 (
    .in0(R0_q), .in1(R2_q), .out(multiplexer_5_out));  // open: sel
  Multiplexer #(.width(4), .enable("false")) multiplexer_6 (
    .in0(R1_q), .in1(R3_q), .out(multiplexer_6_out));  // open: sel
  Comparator #(.width(4), .mode("unsigned")) comparator_1 (
    .a(multiplexer_5_out), .b(multiplexer_6_out), .lt(comparator_1_lt));  // open: gt, eq

  // Notes on the sheet:
  //   src0
  //   src1
  //   src2
  //   src3
  //   m0
  //   m1
endmodule
