// Logisim project datapath.circ as structural Verilog: 4 circuits, main circuit main
module main (
  input  [7:0] din,
  input  en_in,
  input  en_out,
  input  rst,
  input  clk,
  output [7:0] dout,
  output [4:0] count
);

  wire addr_src, control_1_out_6, control_1_out_7, control_1_out_8, control_1_out_9, control_1_out_10,
       control_1_out_11, control_1_out_12, edge_1_out_2, edge_2_out_2, en_ctr, en_head, en_ram, en_tail,
       inc_dec, we_ram;
  wire [3:0] adder_1_out, adder_2_out, head_q, multiplexer_2_out, tail_q;
  wire [4:0] adder_3_out, multiplexer_1_out;

  \edge  edge_1 (.in_1(en_in), .out_2(edge_1_out_2));
  \edge  edge_2 (.in_1(en_out), .out_2(edge_2_out_2));
  Adder #(.width(4)) adder_1 (.a(head_q), .b(4'b0001), .out(adder_1_out));  // open: cin, cout
  Adder #(.width(4)) adder_2 (.a(tail_q), .b(4'b0001), .out(adder_2_out));  // open: cin, cout
  control control_1 (
    .in_1(edge_1_out_2), .in_2(edge_2_out_2), .in_3(rst), .in_4(clk), .out_6(control_1_out_6),
    .out_7(control_1_out_7), .out_8(control_1_out_8), .out_9(control_1_out_9), .in_5(count),
    .out_10(control_1_out_10), .out_11(control_1_out_11), .out_12(control_1_out_12));
  Register #(.width(4)) head (.D(adder_1_out), .en(en_head), .Q(head_q), .clr(rst));  // open: clk
  Register #(.width(4)) tail (.D(adder_2_out), .en(en_tail), .Q(tail_q), .clr(rst));  // open: clk
  Multiplexer #(.width(5), .enable("false")) multiplexer_1 (
    .in0(5'b00001), .in1({5{1'b1}}), .out(multiplexer_1_out), .sel(inc_dec));
  Multiplexer #(.width(4), .enable("false")) multiplexer_2 (
    .in0(head_q), .in1(tail_q), .out(multiplexer_2_out), .sel(addr_src));
  Adder #(.width(5)) adder_3 (.a(count), .b(multiplexer_1_out), .out(adder_3_out));  // open: cin, cout
  mem mem_1 (.addr(multiplexer_2_out), .din(din), .we(we_ram), .en(en_ram), .dout(dout));  // open: clk
  Register #(.width(5)) counter (.D(adder_3_out), .en(en_ctr), .Q(count), .clr(rst));  // open: clk
endmodule

module mem (
  input  [3:0] addr,
  input  [7:0] din,
  input  we,
  input  en,
  input  clk,
  output [7:0] dout
);

  wire and_1_out;

  and and_1 (and_1_out, we, en);
  RAM #(.addrWidth(4), .bus("separate")) ram_1 (
    .addr(addr), .din(din), .data(dout), .str(and_1_out), .clk(clk), .ld(en));  // open: sel, clr
endmodule

module \edge  (
  input  in_1,
  output out_2
);


  assign out_2 = in_1;
endmodule

module control (
  input  in_1,
  input  in_2,
  input  in_3,
  input  in_4,
  input  [4:0] in_5,
  output out_6,
  output out_7,
  output out_8,
  output out_9,
  output out_10,
  output out_11,
  output out_12
);
endmodule
